# Fritzing sketch SerialBlink (saved by Fritzing 0.9.2b)
breadboards: 2

parts:
  부품1 = Arduino Uno (Rev3)
  LED1 = smd LED [color="Red (633nm)" package="0805 [SMD]"]
  LED2 = smd LED [color="Red (633nm)" package="0805 [SMD]"]
  LED3 = smd LED [color="Red (633nm)" package="0805 [SMD]"]
  LED4 = smd LED [color="Red (633nm)" package="0805 [SMD]"]

nets:
  N1: 부품1.D4, LED1.anode
  N2: 부품1.D5_PWM, LED2.anode
  N3: 부품1.D6_PWM, LED3.anode
  N4: 부품1.D7, LED4.anode
  N5: LED1.cathode, LED2.cathode, LED3.cathode, LED4.cathode
